# Fritzing sketch circuit (saved by Fritzing 0.8.7b)

parts:
  Mod1 = Nano-V3-0-IO-Expansion-Adapter
  Componente1 = Arduino Nano (Rev3.0) (ICSP)
  S1 = Pushbutton [package="[SMD]"]
  S2 = Pushbutton [package="[SMD]"]
  S3 = Pushbutton [package="[SMD]"]
  S4 = Pushbutton [package="[SMD]"]
  J1 = Basic Servo  # not connected
  J2 = Basic Servo  # not connected
  J3 = Basic Servo  # not connected
  J4 = Basic Servo
  Part3 = Bluetooth HC-05 Macho
  R1 = Resistor [tolerance=±5% resistance=1k package=THT]
  R2 = Resistor [tolerance=±20% resistance=2.2k package=THT]
  R3 = Rotary Potentiometer (Small) [maximum_resistance=100kΩ package=THT]
  R4 = Rotary Potentiometer (Small) [maximum_resistance=100kΩ package=THT]
  R5 = Rotary Potentiometer (Small) [maximum_resistance=100kΩ package=THT]
  R6 = Rotary Potentiometer (Small) [maximum_resistance=100kΩ package=THT]
  Componente2 = Thumb Joystick
  Componente3 = Thumb Joystick
  Bat1 = battery_holder_dual_18650 [part_number=TBH-18650-2A-P]
  S5 = SPST Switch [package=r_sw_th]
  Power_plug1 = Power plug
  CONN1 = USB connector [package=THT]  # not connected
  LED1 = LED - 5mm [color="Red (633nm)" package="5 mm [THT]"]  # not connected
  R7 = Resistor [tolerance=±5% resistance=220 package=THT]

nets:
  N1: Mod1.RST, Componente1.RESET
  VCC: Mod1.VCC, Componente1.5V, Part3.VCC, R3.leg2
  GND: Mod1.GND, Componente1.GND, Part3.GND, R2.Pin_1, R3.leg1, R7.Pin_1
  VIN: Mod1.VIN, Componente1.VIN
  N2: Mod1.A0, Componente1.A0, R3.wiper
  N3: Mod1.A1, Componente1.A1, R4.wiper
  N4: Mod1.A2, Componente1.A2, R5.wiper
  N5: Mod1.A3, Componente1.A3, R6.wiper
  N6: Mod1.A4/SDA, Componente1.A4, Componente2.HORZ
  N7: Mod1.A5/SCL, Componente1.A5, Componente2.SEL
  N8: Mod1.A6, Componente1.A6, Componente3.HORZ
  N9: Mod1.A7, Componente1.A7, Componente3.SEL
  N10: Mod1.D13/SCK, Componente1.D13/SCK
  N11: Mod1.NC, Componente1.3V3
  N12: Mod1.AREF, Componente1.AREF
  N13: Mod1.D12/MISO, Componente1.D12/MISO
  N14: Mod1.D11_PWM/MOSI, Componente1.D11/MOSI, Part3.TXD
  N15: Mod1.D10_PWM/SS, Componente1.D10, R1.Pin_0
  N16: Mod1.D9_PWM, Componente1.D9, S1.Pin_4
  N17: Mod1.D8, Componente1.D8, S4.Pin_3, S4.Pin_4
  N18: Mod1.D7, Componente1.D7, S3.Pin_3, S3.Pin_4
  N19: Mod1.D6_PWM, Componente1.D6, S2.Pin_3, S2.Pin_4
  N20: Mod1.D5_PWM, Componente1.D5
  N21: Mod1.D4, Componente1.D4
  N22: Mod1.D3_PWM, Componente1.D3
  N23: Mod1.D2, Componente1.D2
  N24: Mod1.D0/RX#64, Mod1.D1/TX#129, Componente1.D0/RX
  N25: Mod1.D1/TX#65, Mod1.D0/RX#128, Componente1.D1/TX
  N26: S1.Pin_1, S1.Pin_2, S2.Pin_1, S2.Pin_2, S3.Pin_1, S4.Pin_1, J4.gnd
  N27: Part3.RXD, R2.Pin_0
  N28: Bat1.+#0, S5.P, Power_plug1.GND
  N29: Bat1.+#2, Bat1.+#3, S5.O, Power_plug1.VCC

custom parts:
  Nano-V3-0-IO-Expansion-Adapter: Nano V3.0 IO Expansion Adapter Shield. Note pcb view has been supressed as not useful. You can drag a Nano over the Nano connectors and it will connect and appear in schematic (although at present due to a bug, routing will not show as complete in breadboard).
  battery_holder_dual_18650: TBH-18650-2A-P dual 18650 battery holder.
