# Fritzing sketch shield-pot (saved by Fritzing 0.8.7b)
perfboards: 1

parts:
  Componente1 = Arduino Uno (Rev3)  # not connected
  U1 = POT [package=alps_pot]
  J4 = male pin header, 6 pins [form="♂ (male)"]  # not connected
  J1 = male pin header, 8 pins [form="♂ (male)"]  # not connected
  J3 = male pin header, 8 pins [form="♂ (male)"]
  J2 = male pin header, 10 pins [form="♂ (male)"]  # not connected
  U2 = POT [package=alps_pot]
  U3 = POT [package=alps_pot]
  U4 = POT [package=alps_pot]
  S1 = Pushbutton [package="[THT]"]
  S2 = Pushbutton [package="[THT]"]
  S3 = Pushbutton [package="[THT]"]
  S4 = Pushbutton [package="[THT]"]
  J5 = male pin header, 3 pins [form="♂ (male)"]
  J6 = male pin header, 3 pins [form="♂ (male)"]  # not connected
  J7 = male pin header, 3 pins [form="♂ (male)"]  # not connected
  J8 = male pin header, 3 pins [form="♂ (male)"]
  C2 = Electrolytic Capacitor [capacitance=100nF package="0405 [SMD, electrolytic]"]  # not connected

nets:
  N1: U1.A, U3.A
  N2: J3.pin3, S4.Pin_1, S4.Pin_2
  N3: J3.pin4, S3.Pin_1, S3.Pin_2
  N4: J3.pin5, S2.Pin_1, S2.Pin_2
  N5: J3.pin6, S1.Pin_1, S1.Pin_2
  N6: U2.E, U3.E, U4.E
  N7: S1.Pin_3, S1.Pin_4
  N8: S2.Pin_3, S2.Pin_4
  N9: S3.Pin_3, S3.Pin_4, S4.Pin_3, S4.Pin_4
  N10: J5.pin2, J8.pin2
  N11: J5.pin3, J8.pin3

notes:
  9  8     7  6
  9 8  7  6
